// Digital circuit angstrom-cpu.dig as structural Verilog
module angstrom_cpu (
  input  CLK,
  input  in_3,
  input  in_4,
  input  in_5,
  input  in_6,
  input  [11:0] in_8,
  input  in_9,
  input  in_10,
  input  in_11,
  input  in_13,
  output [11:0] out_2,
  output out_7,
  output [3:0] out_12
);

  wire decoder_1_out_0, decoder_1_out_1, decoder_1_out_2, decoder_1_out_3, decoder_1_out_4, decoder_1_out_5,
       decoder_1_out_6, decoder_1_out_7, decoder_1_out_8, decoder_1_out_9, decoder_1_out_10,
       decoder_1_out_11, decoder_1_out_12, decoder_1_out_13, decoder_1_out_14, decoder_1_out_15,
       notconnected_3_out, notconnected_4_out, notconnected_5_out;
  wire [3:0] Flags_q, notconnected_2_out, undriven;
  wire [7:0] ACC_q, add_1_s, undriven_2;
  wire [11:0] notconnected_1_out, PC_out;
  wire [15:0] PGM_d;
  wire [15:12] IR_q;

  RAMDualPort #(.AddrBits(12), .Bits(4)) ramdualport_1 (
    .A(notconnected_1_out), .Din(notconnected_2_out), .str(notconnected_3_out), .C(CLK),
    .ld(notconnected_4_out), .D(out_12));
  // NotConnected on notconnected_1_out
  // NotConnected on notconnected_2_out
  // NotConnected on notconnected_3_out
  // NotConnected on notconnected_4_out
  Add #(.Bits(8)) add_1 (.a(ACC_q), .b(undriven_2), .c_i(1'b0), .s(add_1_s), .c_o(undriven[2]));
  Register #(.Bits(8)) ACC (.D(add_1_s), .C(CLK), .en(notconnected_5_out), .Q(ACC_q));
  // NotConnected on notconnected_5_out
  CounterPreset #(.Bits(12)) PC (
    .en(in_11), .C(CLK), .dir(in_5), .in(in_8), .ld(in_9), .clr(in_10), .out(PC_out), .ovf(out_7));
  // Probe on PC_out
  ROM #(.AddrBits(12), .isProgramMemory("true"), .Bits(16)) PGM (.A(PC_out), .sel(in_3), .D(PGM_d));
  Register #(.Bits(4)) Flags (.D(undriven), .C(CLK), .en(in_13), .Q(Flags_q));
  Register #(.Bits(16)) IR (.D(PGM_d), .C(CLK), .en(in_4), .Q({IR_q, out_2}));
  Decoder #(.Selector_Bits(4)) decoder_1 (
    .sel(IR_q), .out_0(decoder_1_out_0), .out_1(decoder_1_out_1), .out_2(decoder_1_out_2),
    .out_3(decoder_1_out_3), .out_4(decoder_1_out_4), .out_5(decoder_1_out_5), .out_6(decoder_1_out_6),
    .out_7(decoder_1_out_7), .out_8(decoder_1_out_8), .out_9(decoder_1_out_9), .out_10(decoder_1_out_10),
    .out_11(decoder_1_out_11), .out_12(decoder_1_out_12), .out_13(decoder_1_out_13),
    .out_14(decoder_1_out_14), .out_15(decoder_1_out_15));

  assign in_6 = in_5;

  // Notes on the sheet:
  //   in_3: default 1
  //   in_4: default 1
  //   in_5: default 1
  //   in_6: default 1
  //   in_11: default 1
  //   in_13: default 1
  //   contents of PGM (hex, n*v repeats v):
  //   0,1000,0,1000
  //   Opcode
  //   Instruction Decoder
  //   Args
endmodule
