// Digital circuit angstrom-cpu.dig as structural Verilog
module angstrom_cpu (
  input  CLK,
  output [7:0] OUT,
  output [7:0] OUT_AOB,
  output [1:0] OUT_flags,
  output [15:0] OUT_INS,
  output [11:0] OUT_PC,
  output [5:0] OUT_CTRL,
  output [7:0] OUT_AIB,
  output [7:0] OUT_ALUA,
  output [7:0] OUT_ALUB
);

  wire add_1_c_o, and_1_out, and_2_out, and_3_out, and_4_out, and_5_out, and_7_out, and_8_out, nor_1_out,
       not_1_out, or_1_out, or_2_out, or_4_out, PC_ovf, sub_1_c_o;
  wire [1:0] nor_2_out;
  wire [2:0] driver_4_out, pulldown_3_out;
  wire [3:0] driver_11_out, pulldown_5_out, ramdualport_1_d;
  wire [7:0] add_1_s, and_6_out, dipswitch_8_out, INP_q, LSL_out, LSR_out, multiplexer_2_out, or_3_out,
       pulldown_1_out, sub_1_s, xor_1_out;

  and and_1 (and_1_out, OUT_flags[0], not_1_out);
  Register #(.Bits(8)) INP (.D(dipswitch_8_out), .C(CLK), .en(OUT_CTRL[1]), .Q(INP_q));
  Register #(.Bits(8)) u_OUT (.D(pulldown_1_out), .C(CLK), .en(OUT_CTRL[0]), .Q(OUT));
  or or_1 (or_1_out, and_1_out, and_2_out);
  and and_2 (and_2_out, OUT_flags[1], pulldown_3_out[0]);
  not not_1 (not_1_out, pulldown_3_out[0]);
  PullDown #(.Bits(8)) pulldown_1 (.out(pulldown_1_out));
  assign OUT_AIB = OUT_CTRL[1] ? INP_q : 8'bz;  // Driver driver_1
  assign pulldown_1_out = OUT_CTRL[0] ? OUT_ALUB : 8'bz;  // Driver driver_2
  and and_3 (and_3_out, pulldown_3_out[0], pulldown_3_out[1], pulldown_3_out[2]);
  PullDown #(.Bits(8)) pulldown_2 (.out(OUT_AIB));
  and and_4 (and_4_out, or_1_out, OUT_CTRL[4]);
  and and_5 (and_5_out, OUT_CTRL[4], and_3_out);
  DipSwitch dipswitch_1 (.out(dipswitch_8_out[1]));
  DipSwitch dipswitch_2 (.out(dipswitch_8_out[0]));
  DipSwitch dipswitch_3 (.out(dipswitch_8_out[2]));
  DipSwitch dipswitch_4 (.out(dipswitch_8_out[3]));
  or or_2 (or_2_out, and_4_out, and_5_out);
  DipSwitch dipswitch_5 (.out(dipswitch_8_out[4]));
  DipSwitch dipswitch_6 (.out(dipswitch_8_out[5]));
  DipSwitch dipswitch_7 (.out(dipswitch_8_out[6]));
  DipSwitch dipswitch_8 (.out(dipswitch_8_out[7]));
  PullDown #(.Bits(3)) pulldown_3 (.out(pulldown_3_out));
  Multiplexer #(.Selector_Bits(3), .Bits(6)) multiplexer_1 (
    .sel(pulldown_3_out), .in_0(6'b001000), .in_1(6'b100000), .in_2(6'b000100), .in_3(6'b000010),
    .in_4(6'b000001), .in_5(6'b010000), .in_6(6'b010000), .in_7(6'b010000), .out(OUT_CTRL));
  assign OUT_ALUA = nor_1_out ? OUT_INS[7:0] : 8'bz;  // Driver driver_3
  PullDown #(.Bits(8)) pulldown_4 (.out(OUT_ALUA));
  assign OUT_ALUA = ~nor_1_out ? {4'b0000, pulldown_5_out} : 8'bz;  // DriverInvSel driverinvsel_1
  nor nor_1 (nor_1_out, driver_4_out[0], driver_4_out[1], driver_4_out[2]);
  Add #(.Bits(8)) add_1 (.a(OUT_ALUA), .b(OUT_ALUB), .c_i(OUT_flags[1]), .s(add_1_s), .c_o(add_1_c_o));
  Sub #(.Bits(8)) sub_1 (.a(OUT_ALUA), .b(OUT_ALUB), .c_i(OUT_flags[1]), .s(sub_1_s), .c_o(sub_1_c_o));
  assign and_6_out = OUT_ALUA & OUT_ALUB;  // And and_6, 8 bits wide
  assign or_3_out = OUT_ALUA | OUT_ALUB;  // Or or_3, 8 bits wide
  assign xor_1_out = OUT_ALUA ^ OUT_ALUB;  // XOr xor_1, 8 bits wide
  BarrelShifter #(.Bits(8)) LSL (.in(OUT_ALUA), .shift(4'b0001), .out(LSL_out));
  BarrelShifter #(.Bits(8), .direction("right")) LSR (.in(OUT_ALUA), .shift(4'b0001), .out(LSR_out));
  Multiplexer #(.Selector_Bits(3), .Bits(8)) multiplexer_2 (
    .sel(driver_4_out), .in_0(add_1_s), .in_1(add_1_s), .in_2(sub_1_s), .in_3(and_6_out), .in_4(or_3_out),
    .in_5(xor_1_out), .in_6(LSL_out), .in_7(LSR_out), .out(multiplexer_2_out));
  assign driver_4_out = OUT_INS[15] ? OUT_INS[14:12] : 3'bz;  // Driver driver_4
  and and_7 (and_7_out, driver_4_out[0], ~driver_4_out[1], ~driver_4_out[2]);  // And
  or or_4 (or_4_out, nor_1_out, and_7_out);
  assign nor_2_out[1] = or_4_out ? add_1_c_o : 1'bz;  // Driver driver_5
  assign pulldown_3_out = ~OUT_INS[15] ? OUT_INS[14:12] : 3'bz;  // DriverInvSel driverinvsel_2
  assign OUT_AIB = OUT_CTRL[5] ? OUT_INS[7:0] : 8'bz;  // Driver driver_6
  and and_8 (and_8_out, driver_4_out[0], ~driver_4_out[1], driver_4_out[2]);  // And
  assign nor_2_out[1] = and_8_out ? sub_1_c_o : 1'bz;  // Driver driver_7
  CounterPreset #(.Bits(12)) PC (
    .en(1'b1), .C(CLK), .dir(1'b0), .in(OUT_INS[11:0]), .ld(or_2_out), .clr(1'b0), .out(OUT_PC), .ovf(PC_ovf));
  PullDown #(.Bits(4)) pulldown_5 (.out(pulldown_5_out));
  assign OUT_AIB = OUT_INS[15] ? multiplexer_2_out : 8'bz;  // Driver driver_8
  assign pulldown_5_out = OUT_CTRL[2] ? ramdualport_1_d : 4'bz;  // Driver driver_9
  PullDown #(.Bits(8)) pulldown_6 (.out(OUT_AIB));
  ROM #(.AddrBits(12), .isProgramMemory("true"), .Bits(16)) PGM (.A(OUT_PC), .sel(1'b1), .D(OUT_INS));
  nor nor_2 (nor_2_out[0], OUT_AIB[0], OUT_AIB[1], OUT_AIB[2], OUT_AIB[3], OUT_AIB[4], OUT_AIB[5], OUT_AIB[6], OUT_AIB[7]);
  Register #(.Bits(2)) FL (.D(nor_2_out), .C(CLK), .en(OUT_INS[15]), .Q(OUT_flags));
  assign OUT_AIB = OUT_CTRL[2] ? {OUT_ALUB[7:4], ramdualport_1_d} : 8'bz;  // Driver driver_10
  Register #(.Bits(8)) ACC (.D(OUT_AIB), .C(CLK), .en(1'b1), .Q(OUT_ALUB));
  RAMDualPort #(.AddrBits(12), .Bits(4)) ramdualport_1 (
    .A(OUT_INS[11:0]), .Din(driver_11_out), .str(OUT_CTRL[3]), .C(CLK), .ld(OUT_CTRL[2]), .D(ramdualport_1_d));
  assign driver_11_out = OUT_CTRL[3] ? OUT_ALUB[3:0] : 4'bz;  // Driver driver_11
  PullDown #(.Bits(4)) pulldown_7 (.out(ramdualport_1_d));

  assign OUT_AOB = OUT_ALUB;
  // also tied to GND on the sheet: {PC_ovf, OUT_flags[0], OUT_INS[8], OUT_INS[9], OUT_INS[10], OUT_INS[11]}

  // Notes on the sheet:
  //   BRZ
  //   Z
  //   C
  //   Conditional Jump
  //   BRC
  //   Flags
  //   CTRL_INP
  //   CTRL_OUT
  //   Instruction
  //   Unconditional Jump
  //   CTRL_IMM
  //   CTRL_JMP
  //   CTRL_MR
  //   CTRL_MW
  //   IMM
  //   MEM
  //   ALU_A
  //   ALU_B
  //   AIB
  //   AOB
  //   ADI
  //   JMP
  //   OUT
  //   INP
  //   STA
  //   LDI
  //   LDA
  //   ALU_OP
  //   Immediate
  //   ADD
  //   ALU Ops
  //   Other Ops
  //   SUB
  //   C_IN
  //   CTRL_ALU
  //   Z check
  //   C_OUT
  //   ALU
  //   PGM loads ADI.hex
  //   RAM
  //   Op
  //   Args
endmodule
